# Fritzing sketch Keyboard (saved by Fritzing 0.7.4b)
breadboards: 1

parts:
  Arduino1 = Arduino
  J1 = Piezo Speaker
  LED1 = LED - 5mm [color="Red (633nm)" package="5 mm [THT]"]
  R2 = Resistor [tolerance=±5% resistance=220 package=THT]
  R3 = Resistor [tolerance=±5% resistance=220 package=THT]
  R4 = Resistor [tolerance=±5% resistance=220 package=THT]
  R5 = Resistor [tolerance=±5% resistance=220 package=THT]
  LED2 = LED - 5mm [color="Red (633nm)" package="5 mm [THT]"]
  LED3 = LED - 5mm [color="Red (633nm)" package="5 mm [THT]"]
  LED4 = LED - 5mm [color="Red (633nm)" package="5 mm [THT]"]

nets:
  N1: Arduino1.D11, Arduino1.GND, J1.pin1, J1.pin2, LED1.cathode, LED1.anode, R2.Pin_1, R3.Pin_1, R4.Pin_1, R5.Pin_1, LED2.cathode, LED2.anode, LED3.cathode, LED3.anode, LED4.cathode, LED4.anode
  N2: Arduino1.D10, R2.Pin_0
  N3: Arduino1.D9, R3.Pin_0
  N4: Arduino1.D8, R4.Pin_0
  N5: Arduino1.D7, R5.Pin_0

notes:
  BUTTONS
