# Fritzing sketch Morse (saved by Fritzing 0.7.4b)
breadboards: 1

parts:
  Arduino1 = Arduino
  R8 = Resistor [resistance=220 tolerance=±5% package=THT]
  LED11 = LED - 5mm [color="Red (633nm)" package="5 mm [THT]"]

nets:
  N1: Arduino1.D13, R8.Pin_1
  N2: Arduino1.GND, LED11.cathode
  N3: R8.Pin_0, LED11.anode
