# Fritzing sketch ButtonLed (saved by Fritzing 0.7.4b)
breadboards: 1

parts:
  Arduino2 = Arduino
  R5 = Resistor [resistance=220 tolerance=±5% package=THT]
  LED3 = LED - 5mm [color="Red (633nm)" package="5 mm [THT]"]
  R6 = Resistor [resistance=10k tolerance=±5% package=THT]
  S2 = Pushbutton [package=THT]

nets:
  N1: Arduino2.D3, R5.Pin_1
  N2: R5.Pin_0, LED3.anode
  N3: R6.Pin_1, S2.leg1

// code stored in the sketch: Blink.ino
/*
  Blink
  Turns on an LED on for one second, then off for one second, repeatedly.
 
  This example code is in the public domain.
 */

void setup() {                
  // initialize the digital pin as an output.
  // Pin 13 has an LED connected on most Arduino boards:
  pinMode(13, OUTPUT);     
}

void loop() {
  digitalWrite(13, HIGH);   // set the LED on
  delay(1000);              // wait for a second
  digitalWrite(13, LOW);    // set the LED off
  delay(1000);              // wait for a second
}
