# Fritzing sketch TemperaturSensorLM35 (saved by Fritzing 0.7.4b)
breadboards: 1

parts:
  T1 = LM35 Temperature Sensor [package="TO92 [THT]"]
  R1 = Resistor [tolerance=±5% resistance=220 package=THT]
  LED1 = LED - 5mm [color="Green (555nm)" package="5 mm [THT]"]
  R2 = Resistor [tolerance=±5% resistance=220 package=THT]
  R3 = Resistor [tolerance=±5% resistance=220 package=THT]
  R4 = Resistor [tolerance=±5% resistance=220 package=THT]
  R5 = Resistor [tolerance=±5% resistance=220 package=THT]
  R6 = Resistor [tolerance=±5% resistance=220 package=THT]
  LED2 = LED - 5mm [color="Green (555nm)" package="5 mm [THT]"]
  LED3 = LED - 5mm [color="Yellow (595nm)" package="5 mm [THT]"]
  LED4 = LED - 5mm [color="Yellow (595nm)" package="5 mm [THT]"]
  LED5 = LED - 5mm [color="Red (633nm)" package="5 mm [THT]"]
  LED6 = LED - 5mm [color="Red (633nm)" package="5 mm [THT]"]
  Arduino1 = Arduino

nets:
  N1: T1.+Vs, Arduino1.+5V
  N2: T1.Vout, Arduino1.A0
  GND: T1.GND, R1.Pin_0, R2.Pin_0, R3.Pin_0, R4.Pin_0, R5.Pin_0, R6.Pin_0, Arduino1.GND
  N3: R1.Pin_1, LED1.anode
  N4: LED1.cathode, Arduino1.D2
  N5: R2.Pin_1, LED2.anode
  N6: R3.Pin_1, LED3.anode
  N7: R4.Pin_1, LED4.anode
  N8: R5.Pin_1, LED5.anode
  N9: R6.Pin_1, LED6.anode
  N10: LED2.cathode, Arduino1.D3
  N11: LED3.cathode, Arduino1.D4
  N12: LED4.cathode, Arduino1.D5
  N13: LED5.cathode, Arduino1.D6
  N14: LED6.cathode, Arduino1.D7

notes:
  Digital Thermometer
  get the code from here
  Digital Thermometer with LM35

// code stored in the sketch: TemperaturSensorLM35.ino
/*

  Sensing the Temperature with the LM35
  Fritzing.org
  
  This script will output the sensed temperature of the LM35 from 20 to 32°C by LEDs.
  
  inspired by
  ladyada http://www.ladyada.net/learn/sensors/tmp36.html
  pscmpf http://pscmpf.blogspot.com/2008/12/arduino-lm35-sensor.html
  
*/

float temperature;                        // stores the temperature
int sensorPin = 0;                        // pin where the sensor is connected to
int startTemp=20;                         // the start temperature > at this temperature, no LED will light up

void setup()
{
  Serial.begin(9600);                     // initialisation of the serial connection
  for (int i=2;i<8; i++){                // output channels from 2 to 7
    pinMode(i,OUTPUT);                    // pin is a output
  }
}

void loop()
{
  temperature = analogRead(sensorPin);    // reading analog sensor value
  temperature = temperature*0.488;        // correcting to °C 

  for (int i=0;i<8; i++){
    if (temperature>((i*2)+startTemp)){       // switch LED on, if temperature is higher than starttemp + (LED number*2)
      digitalWrite(i,HIGH);
    } 
    else {
      digitalWrite(i,LOW);                // else, switch it off
    }
  }

  Serial.print(temperature);Serial.println(" °C");  // send the temperarue to the serial monitor
  delay(500);                             // just wait a little
}
