# Fritzing sketch ProtoRover (saved by Fritzing 0.7.4b)
breadboards: 1

parts:
  Arduino1 = Arduino
  J1 = Basic Servo
  J2 = Basic Servo
  J3 = Basic Servo
  J4 = Basic Servo
  J5 = Basic Servo
  J6 = Basic Servo

nets:
  N1: Arduino1.D11, J6.pulse
  N2: Arduino1.D10, J4.pulse
  N3: Arduino1.D9, J2.pulse
  N4: Arduino1.D5, J3.pulse
  N5: Arduino1.D3, J1.pulse
  VCC: J1.vcc, J2.vcc, J3.vcc, J4.vcc, J5.vcc, J6.vcc
  GND: J2.gnd, J3.gnd, J4.gnd, J5.gnd, J6.gnd
