# Fritzing sketch schedariconoscimento (saved by Fritzing 0.7.4b)
breadboards: 1

parts:
  Arduino2 = Arduino
  LED2 = RGB LED (com. anode, rbg) [package="5 mm [THT]"]
  R4 = Resistor [tolerance=±5% resistance=220 package=THT]  # not connected
  R5 = Resistor [tolerance=±5% resistance=220 package=THT]
  R6 = Resistor [tolerance=±5% resistance=220 package=THT]
  RFID_Evaluation_Shield2 = RFID  # not connected
  C1 = Ceramic Capacitor [capacitance=100nF package="100 mil [THT, multilayer]"]
  R7 = Resistor [tolerance=±5% resistance=220 package=THT]
  LED3 = LED - 5mm [color="Red (633nm)" package="5 mm [THT]"]
  R8 = Resistor [tolerance=±5% resistance=220 package=THT]
  VCC1 = Battery  # not connected

nets:
  N1: Arduino2.D5, R5.Pin_0
  N2: Arduino2.D4, R7.Pin_1
  N3: Arduino2.D3, R6.Pin_0
  N4: Arduino2.+5V, LED2.common_anode
  N5: Arduino2.A0, C1.1
  N6: Arduino2.A2, R8.Pin_0
  N7: LED2.red_cathode, R6.Pin_1
  N8: LED2.blue_cathode, R5.Pin_1
  N9: C1.0, R8.Pin_1
  N10: R7.Pin_0, LED3.anode

notes:
  RFID module = SM130
  Bisogna saldare i componenti sulla shield qua a fianco (modulo e pin) e poi basta attaccarla ad Arduino
  Pin 7 e 8 usati per la comunicazione con la shield
  SOUND SENSOR
  BIANCO: Vin
  NERO: GROUND
  ROSSO: 5v
  PIR SENSOR
  BLACK: Vin sensore
  BROWN GROUND
  ROSSO: 12v
  12V
