# Fritzing sketch Progetto_01 (saved by Fritzing 0.6.3b)
breadboards: 1

parts:
  Arduino1 = Arduino
  S1 = Pushbutton [package="[THT]"]
  S5 = Pushbutton [package="[THT]"]
  S6 = Pushbutton [package="[THT]"]
  R1 = Resistor [tolerance=±5% resistance=330 package=THT]
  LED1 = LED - 5mm [color="Red (633nm)" package="5 mm [THT]"]
  LED2 = LED - 5mm [color="Red (633nm)" package="5 mm [THT]"]
  LED3 = LED - 5mm [color="Red (633nm)" package="5 mm [THT]"]
  R2 = Resistor [tolerance=±5% resistance=330 package=THT]
  R3 = Resistor [tolerance=±5% resistance=330 package=THT]

nets:
  N1: Arduino1.D12, S1.Pin_1, S1.Pin_2
  N2: Arduino1.D11, S5.Pin_1, S5.Pin_2
  N3: Arduino1.D10, S6.Pin_1, S6.Pin_2
  N4: Arduino1.D6, R1.Pin_1
  N5: Arduino1.D5, R2.Pin_1
  N6: Arduino1.D3, R3.Pin_1
  N7: Arduino1.GND, S1.Pin_3, S1.Pin_4, S5.Pin_3, S5.Pin_4, S6.Pin_3, S6.Pin_4, LED1.cathode, LED2.cathode, LED3.cathode
  N8: R1.Pin_0, LED1.anode
  N9: LED2.anode, R2.Pin_0
  N10: LED3.anode, R3.Pin_0

notes:
  - Arduino UNO
  - Pulsante (3 pz.)
  - Resistenza 470 ohm (3 pz.)
  - LED (3 pz.)
  - Mini Breadboard
