# Fritzing sketch Progetto_03 (saved by Fritzing 0.6.3b)
breadboards: 1

parts:
  Arduino1 = Arduino
  M1 = DC Motor
  S1 = Pushbutton [package="[THT]"]
  S2 = Pushbutton [package="[THT]"]
  Q1 = NPN-Transistor [package="TO92 [THT]"]

nets:
  N1: Arduino1.D11, S1.Pin_1, S1.Pin_2
  N2: Arduino1.D10, S2.Pin_1, S2.Pin_2
  N3: Arduino1.D3, Q1.B
  N4: Arduino1.3V3, M1.pin_2
  N5: Arduino1.GND, S1.Pin_3, S1.Pin_4, S2.Pin_3, S2.Pin_4, Q1.C
  N6: M1.pin_1, Q1.E

notes:
  - Arduino UNO
  - BC547
  - Motore 3V
  - Pulsanti (2 pz.)
