# Fritzing sketch Progetto_10 (saved by Fritzing 0.6.3b)
breadboards: 1

parts:
  Arduino1 = Arduino
  S1 = Tilt Switch [part_number=MERS4 package=THT]
  J1 = Piezo Speaker

nets:
  N1: Arduino1.D3, J1.pin1
  N2: Arduino1.D2, S1.Pin_1
  N3: Arduino1.+5V, J1.pin2
  N4: Arduino1.GND, S1.Pin_2

notes:
  - Arduino UNO
  - Buzzer senza elettronica
  - Sensore di movimento
  - Mini breadboard
