# Fritzing sketch Progetto_09 (saved by Fritzing 0.6.3b)
breadboards: 1

parts:
  Arduino1 = Arduino
  R1 = Photocell (LDR) [package=THT]
  K1 = Relay [part_number=FRS1B-S package=THT]
  Q1 = NPN-Transistor [package="TO92 [THT]"]
  R2 = Resistor [tolerance=±5% resistance=4.7k package=THT]
  R3 = Resistor [tolerance=±5% resistance=4.7k package=THT]
  D1 = Rectifier Diode [part_number=1N4001 package="300 mil [THT]"]

nets:
  N1: Arduino1.GND, Q1.C, R3.Pin_1
  N2: Arduino1.D2, R2.Pin_0
  N3: Arduino1.+5V, R1.pin_1
  N4: Arduino1.VIN, K1.COIL2, D1.cathode
  N5: Arduino1.A0, R1.pin_0, R3.Pin_0
  N6: K1.COIL1, Q1.E, D1.anode
  N7: K1.C1, K1.C2
  N8: Q1.B, R2.Pin_1

notes:
  - Arduino UNO
  - Relè 12V
  - Resistenza 4,7 kohm (2 pz.)
  - BC547
  - Fotoresistenza
