# Fritzing sketch Progetto_06 (saved by Fritzing 0.6.3b)

parts:
  Arduino1 = Arduino
  LCD1 = LCD screen
  R2 = Slide Potentiometer [maximum_resistance=100kΩ]

nets:
  GND: Arduino1.GND, LCD1.VSS, LCD1.R/W, R2.leg1
  N1: Arduino1.D12, LCD1.RS
  N2: Arduino1.D11, LCD1.E
  N3: Arduino1.D5, LCD1.DB4
  N4: Arduino1.D4, LCD1.DB5
  N5: Arduino1.D3, LCD1.DB6
  N6: Arduino1.D2, LCD1.DB7
  +5V: Arduino1.+5V, LCD1.VDD
  N7: LCD1.V0, R2.wiper

notes:
  - Arduino UNO
  - Display LCD (16x2)
  - Slider 5 kohm
