# Fritzing sketch Progetto_07 (saved by Fritzing 0.6.3b)
breadboards: 1

parts:
  Arduino1 = Arduino
  LCD1 = LCD screen
  R2 = Slide Potentiometer [maximum_resistance=100kΩ]
  Q1 = NPN-Transistor [part_number=DS18B20 package="TO92 [THT]"]
  R1 = Resistor [tolerance=±5% resistance=4.7k package=THT]

nets:
  GND: Arduino1.GND, LCD1.VSS, LCD1.R/W, R2.leg1, Q1.E
  N1: Arduino1.D12, LCD1.RS
  N2: Arduino1.D11, LCD1.E
  N3: Arduino1.D6, Q1.B, R1.Pin_0
  N4: Arduino1.D5, LCD1.DB4
  N5: Arduino1.D4, LCD1.DB5
  N6: Arduino1.D3, LCD1.DB6
  N7: Arduino1.D2, LCD1.DB7
  +5V: Arduino1.+5V, LCD1.VDD, R2.leg2, Q1.C, R1.Pin_1
  N8: LCD1.V0, R2.wiper

notes:
  - Arduino UNO
  - DS18B20
  - Resistenza 4k7
  - Display LCD (16x2)
  - Slider 5 kohm
  - Mini Breadboard
