# Fritzing sketch Progetto_11 (saved by Fritzing 0.6.3b)
breadboards: 1

parts:
  Arduino1 = Arduino
  U1 = mystery part, 3 pins [chip_label=IR38DM spacing=300mil]

nets:
  N1: Arduino1.D6, U1.pin1
  N2: Arduino1.+5V, U1.pin3
  N3: Arduino1.GND, U1.pin2

notes:
  - Arduino UNO
  - Ricevitore IR (IR38DM)
  - Mini breadboard
