# Fritzing sketch Progetto_05 (saved by Fritzing 0.6.3b)
breadboards: 1

parts:
  Arduino1 = Arduino
  R1 = Resistor [tolerance=±5% resistance=4.7k package=THT]
  Q1 = NPN-Transistor [part_number=DS18B20 package="TO92 [THT]"]

nets:
  N1: Arduino1.D2, R1.Pin_0, Q1.B
  N2: Arduino1.+5V, R1.Pin_1, Q1.C
  N3: Arduino1.GND, Q1.E

notes:
  - Arduino UNO
  - DS18B20
  - Resistenza 4k7
  - Mini Breadboard
