# Fritzing sketch Progetto_02 (saved by Fritzing 0.6.3b)
breadboards: 1

parts:
  Arduino1 = Arduino
  S5 = Pushbutton [package="[THT]"]
  S6 = Pushbutton [package="[THT]"]
  LED3 = LED - 5mm [color="Red (633nm)" package="5 mm [THT]"]
  R3 = Resistor [tolerance=±5% resistance=330 package=THT]

nets:
  N1: Arduino1.D11, S5.Pin_1, S5.Pin_2
  N2: Arduino1.D10, S6.Pin_1, S6.Pin_2
  N3: Arduino1.D3, R3.Pin_0
  N4: Arduino1.GND, S5.Pin_3, S5.Pin_4, S6.Pin_3, S6.Pin_4, LED3.cathode
  N5: LED3.anode, R3.Pin_1

notes:
  - Arduino UNO
  - LED
  - Pulsanti (2 pz.)
  - Resistenza 330 ohm
