# Fritzing sketch Progetto_13 (saved by Fritzing 0.6.3b)

parts:
  Arduino1 = Arduino
  J1 = Basic Servo
  R1 = Slide Potentiometer [maximum_resistance=100kΩ]

nets:
  GND: Arduino1.GND, J1.gnd, R1.leg1
  N1: Arduino1.D3, J1.pulse
  +5V: Arduino1.+5V, J1.vcc, R1.leg2
  N2: Arduino1.A0, R1.wiper

notes:
  - Arduino UNO
  - Servo motore 5V
  - Slider 5 kohm
