# Fritzing sketch Progetto_12 (saved by Fritzing 0.6.3b)
breadboards: 1

parts:
  Arduino1 = Arduino
  C1 = Ceramic Capacitor [capacitance=100nF voltage=16V part_number=NTC package="100 mil [THT, multilayer]"]
  R1 = Resistor [tolerance=±5% resistance=4.7k package=THT]

nets:
  N1: Arduino1.+5V, C1.1
  N2: Arduino1.GND, R1.Pin_0
  N3: Arduino1.A0, C1.0, R1.Pin_1

notes:
  - Arduino UNO
  - NTC 5kohm
  - Resistenza 4,7 kohm
  - Mini breadboard
