# Fritzing sketch Progetto_04 (saved by Fritzing 0.6.3b)
breadboards: 1

parts:
  Arduino1 = Arduino
  M1 = DC Motor
  Q1 = NPN-Transistor [package="TO92 [THT]"]
  R1 = Slide Potentiometer [maximum_resistance=5kΩ]

nets:
  N1: Arduino1.GND, Q1.C, R1.leg1
  N2: Arduino1.D3, Q1.B
  N3: Arduino1.3V3, M1.pin_2
  N4: Arduino1.+5V, R1.leg2
  N5: Arduino1.A0, R1.wiper
  N6: M1.pin_1, Q1.E

notes:
  - Arduino UNO
  - BC547
  - Motore 3V
  - Slider 5k
